# Fritzing sketch led-box (saved by Fritzing 0.9.4)
perfboards: 1

parts:
  IC1 = IC, DIP package, 14 pins [chip_label=74AHCT125]
  Power_plug1 = Power plug
  J4 = male pin header, 4 pins [form="♂ (male)"]
  J1 = male pin header, 2 pins [form="♂ (male)"]
  J2 = male pin header, 2 pins [form="♂ (male)"]
  Raspberry_Pi_Zero1 = Raspberry Pi Zero
  U1 = WS2801 [package=sop-14]

nets:
  N1: IC1.pin1, IC1.pin4, IC1.pin7, J2.pin1
  N2: IC1.pin2, Raspberry_Pi_Zero1.GIPO11
  N3: IC1.pin3, J4.pin3, U1.CKI
  N4: IC1.pin5, Raspberry_Pi_Zero1.GIPO10
  N5: IC1.pin6, J4.pin2, U1.SDI
  N6: IC1.pin14, J1.pin1
  N7: Power_plug1.GND, J1.pin2
  N8: Power_plug1.VCC, J2.pin2
  N9: J4.pin1, U1.GND
  N10: J4.pin4, U1.VCC
